// Logisim project киба лаба 1.circ as structural Verilog: 1 circuit, main circuit main
module main (
  input  X4,
  input  X3,
  input  X2,
  input  X1
);

  wire and_1_out, and_2_out, and_3_out, not_1_out, not_2_out, not_3_out, not_4_out, not_5_out, or_1_out,
       or_2_out;

  not not_1 (not_1_out, X2);
  not not_2 (not_2_out, X3);
  not not_3 (not_3_out, X4);
  not not_4 (not_4_out, X4);
  and and_1 (and_1_out, X1, not_1_out, not_2_out, not_3_out);
  and and_2 (and_2_out, X3, not_4_out);
  or or_1 (or_1_out, X2, X3);
  not not_5 (not_5_out, X4);
  or or_2 (or_2_out, and_1_out, and_2_out);
  and and_3 (and_3_out, or_1_out, not_5_out);
  LED led_1 (.in(or_2_out));
  LED led_2 (.in(and_3_out));
  LED led_3 (.in(X4));

  // Notes on the sheet:
  //   Y1
  //   Y2
  //   Y3
endmodule
